# Fritzing sketch wiring (saved by Fritzing 0.9.2b)

parts:
  Part1 = Arduino Nano (Rev3.0)
  R1 = Resistor [tolerance=±5% resistance=220 package=THT]
  LED1 = LED - 3mm [color="Red (633nm)" package="3 mm [THT]"]
  R2 = Resistor [tolerance=±5% resistance=220 package=THT]
  LED2 = LED - 3mm [color="Red (633nm)" package="3 mm [THT]"]
  LedStrip = Neopixel Strip -- Black (30/m)
  R3 = Resistor [tolerance=±5% resistance=330 package=THT]
  Relay = Keyes Relay [package=THT]
  S1 = Pushbutton [package="[SMD]"]
  S2 = Pushbutton [package="[SMD]"]
  NRF24L1 = NRF24L01
  R4 = Rotary Potentiometer (Small) [maximum_resistance=100kΩ package=THT]
  C3 = Ceramic Capacitor [capacitance=10nF package="0805 [SMD, multilayer]"]
  C4 = Electrolytic Capacitor [capacitance=1000µF package="300 mil [THT, electrolytic]"]  # not connected
  U1 = Header 8 [package=1x08_smd]
  S3 = Pushbutton [package="[SMD]"]
  U2 = Header 8 [package=1x08_smd]

nets:
  N1: Part1.RESET, U1.1
  GND: Part1.GND, LED1.cathode, LED2.cathode, LedStrip.GND, Relay.ground, S1.Pin_3, S1.Pin_4, S2.Pin_3, S2.Pin_4, NRF24L1.GND, R4.leg1, C3.0, U1.2, S3.Pin_1, S3.Pin_2, U2.2
  N2: Part1.D2, R3.Pin_1
  N3: Part1.D4, Relay.signal
  N4: Part1.D5, R1.Pin_1
  N5: Part1.D6, R2.Pin_1
  N6: Part1.D7, U1.5
  N7: Part1.D8, U1.6
  N8: Part1.D9, NRF24L1.CE
  N9: Part1.D10, NRF24L1.CSN
  N10: Part1.D11/MOSI, NRF24L1.MOSI
  N11: Part1.D12/MISO, NRF24L1.MISO
  N12: Part1.5V, U1.8
  N13: Part1.A0, C3.1, U1.7
  3V3: Part1.3V3, NRF24L1.VCC
  N14: Part1.D13/SCK, NRF24L1.SCK
  N15: R1.Pin_0, U1.3
  N16: LED1.anode, U2.4
  N17: R2.Pin_0, U1.4
  N18: LED2.anode, U2.3
  N19: LedStrip.Din, R3.Pin_0
  N20: S1.Pin_1, S1.Pin_2, U2.6
  N21: S2.Pin_1, U2.5
  N22: R4.wiper, U2.7
  N23: R4.leg2, U2.8
  N24: S3.Pin_3, U2.1

custom parts:
  Neopixel Strip -- Black (30/m): These NeoPixel strips have 30 digitally-addressable pixel LEDs per meter and are very affordable and are only 12.5 mm wide, 10 mm if you remove the strip from the casing.
  Keyes Relay: The Keyes 5V relay module is suitable for SCM development, home appliance control. It uses a 5V~12V TIL control signal which can control DC / AC signal.
  NRF24L01: NRF24L01 module
